# Fritzing sketch tanduino (saved by Fritzing 0.9.2b)
breadboards: 1

parts:
  Part1 = Arduino Pro Mini v13
  C1 = Electrolytic Capacitor [capacitance=1µF package="100 mil [THT, electrolytic]"]
  VCC1 = Battery block 9V
  GY-1 = GY-271 [part_number=GY-271]
  Part2 = Triple Axis Accelerometer Breakout - ADXL345
  Nokia_5110_LCD_Module1 = Nokia 5110 LCD basado en PCD8544
  S1 = Round Pushbutton
  R3 = Resistor [tolerance=±5% resistance=10k package="0603 [SMD]"]
  R4 = Trimmer Potentiometer [maximum_resistance=10kΩ package=THT]
  U1 = SWITCH-SPST-2 [package=r_sw_th]
  C2 = Capacitor [part_number=100nF package=cap-pth-small2]
  R5 = Resistor [tolerance=±5% resistance=1M package="0603 [SMD]"]
  R6 = Resistor [tolerance=±5% resistance=470k package="0603 [SMD]"]
  U2 = Voltage Regulator [package=to220-adj]
  5mW_Laser1 = 5mW Laser
  J1 = Piezo Speaker
  U3 = Transformer [package=transformer]
  R7 = Trimmer Potentiometer [maximum_resistance=10kΩ package=THT]

nets:
  N1: Part1.A4, GY-1.SDA, Part2.SDA
  N2: Part1.A5, GY-1.SCL, Part2.SCL
  GND: Part1.GND, C1.-, VCC1.-, GY-1.GND, Part2.GND, Nokia_5110_LCD_Module1.GND, S1.leg1, R4.leg1, C2.2, R6.Pin_0, U2.IN, U3.3, R7.leg1
  VCC: Part1.VCC, Part1.A0, C1.+, GY-1.VCC, Part2.VCC, Nokia_5110_LCD_Module1.VCC, U2.OUT
  N3: Part1.A1, R5.Pin_1, R6.Pin_1
  N4: Part1.D13/SCK, Nokia_5110_LCD_Module1.CLK
  N5: Part1.D11_PWM/MOSI, Nokia_5110_LCD_Module1.DIN
  N6: Part1.D10_PWM/SS, Nokia_5110_LCD_Module1.CE
  N7: Part1.D9_PWM, Nokia_5110_LCD_Module1.RST
  N8: Part1.D8, Nokia_5110_LCD_Module1.DC
  N9: Part1.D7, 5mW_Laser1.C
  N10: Part1.D3_PWM, U3.2
  N11: Part1.D2, R3.Pin_1
  N12: VCC1.+, U1.O
  N13: Nokia_5110_LCD_Module1.LIGHT, R4.wiper
  N14: S1.leg0, R3.Pin_0, C2.1
  N15: U1.P, R5.Pin_0, U2.ADJ
  N16: 5mW_Laser1.A, R7.wiper
  N17: J1.pin1, U3.1
  N18: J1.pin2, U3.4

custom parts:
  GY-271: GY-271 - Electronic compass module - 3 Axis Magnetic Field Sensor HMC5883L
  Nokia 5110 LCD basado en PCD8544: Módulo Nokia 5110 LCD basado en el controlador PCD8544. Versión de 8 pines (sólo entrada).
  5mW Laser: 5mW 3.3V 40mA 650nm laser diode
